# Fritzing sketch Analog Zero (saved by Fritzing 0.9.7b)
breadboards: 1

parts:
  Mod1 = Raspberry Pi 4B
  U1 = POT [package=pot_alpha_rv16af-20]
  LED1 = LED - 5mm [color="Red (633nm)" current=0.030 package="5 mm [THT]"]
  R1 = Resistor [tolerance=±5% power=0.25 resistance=330 package=THT]

nets:
  N1: Mod1.3V3, U1.A
  N2: Mod1.GND, U1.E, R1.Pin_0
  N3: Mod1.GPIO17, LED1.anode
  N4: LED1.cathode, R1.Pin_1
