# Fritzing sketch Pico Analog (saved by Fritzing 0.9.7b)
breadboards: 1

parts:
  Mod1 = Raspberry Pi 4B
  U1 = POT [package=pot_alpha_rv16af-20]
  LED1 = LED - 5mm [color="Red (633nm)" current=0.030 package="5 mm [THT]"]
  R1 = Resistor [tolerance=±5% power=0.25 resistance=330 package=THT]
  Mod2 = Raspberry Pi Pico

nets:
  N1: Mod1.GND, R1.Pin_0
  N2: Mod1.GPIO17, LED1.anode
  N3: U1.A, Mod2.pin_36
  N4: U1.S, Mod2.pin_31
  N5: U1.E, Mod2.pin_3, Mod2.pin_8, Mod2.pin_13, Mod2.pin_18, Mod2.pin_23, Mod2.pin_28, Mod2.pin_33, Mod2.pin_38
  N6: LED1.cathode, R1.Pin_1

custom parts:
  Raspberry Pi Pico: Raspberry Pi Pico. Based around the RP2040 microcontroller the Pico is a low cost microcontroller device bringing Raspberry Pi quality, cost, and easy of use to the microcontroller space. Jan 2021, Split part in to two versions: tht (this one) and SMD. This one will drill holes for a .1 in header in pcb to allow plugging in the module as well as providing pads to solder the module to the top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
